// Logisim project Project2Given.circ as structural Verilog: 4 circuits, main circuit main
module main (
);

  wire and_1_out, and_2_out, B0, B1, B2, B3, B4, B5, B6, B7, B8, B9, BL, BU, C0, C1, C2, CLK, L1_l, L1_u,
       not_1_out, or_8_out, P1_b3, R0, R1, R3, R4, Valid;
  wire [2:0] counter_1_q;
  wire [3:0] IB1_c0, P1_b0, register_3_q, register_4_q, register_5_q;

  Button n1 (.out(B1));
  Button n4 (.out(B4));
  Button n7 (.out(B7));
  Button L (.out(BL));
  Button n3 (.out(B3));
  Button n2 (.out(B2));
  Button n6 (.out(B6));
  Button n5 (.out(B5));
  Button n9 (.out(B9));
  Button n8 (.out(B8));
  Button U (.out(BU));
  Button n0 (.out(B0));
  or or_1 (R0, B3, B2, B1);
  or or_2 (R1, B6, B5, B4);
  or or_3 (R3, B9, B8, B7);
  or or_4 (R4, BU, B0, BL);
  or or_5 (C0, B1, B4, B7, BL);
  or or_6 (C1, B2, B5, B8, B0);
  or or_7 (C2, B3, B6, B9, BU);
  Clock clock_1 (.out(CLK));
  nand nand_1 (Valid, IB1_c0[0], IB1_c0[1], IB1_c0[2], IB1_c0[3]);
  // Probe on P1_b0
  Panel P1 (
    .R0(R0), .R1(R1), .R2(R3), .R3(R4), .C0(C0), .C1(C1), .C2(C2), .B0(P1_b0[0]), .B1(P1_b0[1]),
    .B2(P1_b0[2]), .V(P1_b0[3]), .B3(P1_b3));
  LED Press (.in(P1_b3));
  // Probe on IB1_c0
  InputBuffer IB1 (
    .B0(P1_b0[0]), .B1(P1_b0[1]), .B2(P1_b0[2]), .B3(P1_b0[3]), .V(P1_b3), .CLK(not_1_out), .C0(IB1_c0[0]),
    .C1(IB1_c0[1]), .C2(IB1_c0[2]), .C3(IB1_c0[3]));
  not not_1 (not_1_out, CLK);
  Register #(.width(4)) register_1 (.D(register_3_q), .en(Valid), .clk(CLK));  // open: Q, clr
  Lock L1 (.C0(IB1_c0[0]), .C1(IB1_c0[1]), .C2(IB1_c0[2]), .C3(IB1_c0[3]), .CLK(CLK), .L(L1_l), .U(L1_u));
  Counter #(.max('h7), .width(3)) counter_1 (
    .count(or_8_out), .Q(counter_1_q), .up(L1_u), .clk(CLK));  // open: load, D, carry, clr
  or or_8 (or_8_out, L1_l, L1_u);
  Register #(.width(4)) register_2 (.D(register_3_q), .en(Valid), .clk(CLK));  // open: Q, clr
  LED Unlocked (.in(and_1_out));
  and and_1 (and_1_out, ~counter_1_q[0], ~counter_1_q[1], ~counter_1_q[2]);  // AND_Gate
  Register #(.width(4)) register_3 (.D(register_4_q), .en(Valid), .clk(CLK), .Q(register_3_q));  // open: clr
  LED Locked (.in(and_2_out));
  and and_2 (and_2_out, ~counter_1_q[0], ~counter_1_q[1], counter_1_q[2]);  // AND_Gate
  Register #(.width(4)) register_4 (.D(register_5_q), .en(Valid), .clk(CLK), .Q(register_4_q));  // open: clr
  Register #(.width(4)) register_5 (.D(IB1_c0), .en(Valid), .clk(CLK), .Q(register_5_q));  // open: clr
endmodule

module Panel (
  input  R0,
  input  R1,
  input  R2,
  input  R3,
  input  C0,
  input  C1,
  input  C2,
  output B0,
  output B1,
  output B2,
  output V,
  output B3
);

  wire or_1_out, undriven, undriven_2, undriven_3;
  wire [11:0] and_1_out;

  and and_1 (and_1_out[0], R0, C0);
  and and_2 (and_1_out[1], C0, R1);
  and and_3 (and_1_out[2], C0, R2);
  and and_4 (and_1_out[3], C0, R3);
  and and_5 (and_1_out[4], C1, R0);
  and and_6 (and_1_out[5], C1, R1);
  and and_7 (and_1_out[6], C1, R2);
  and and_8 (and_1_out[7], C1, R3);
  and and_9 (and_1_out[8], C2, R0);
  and and_10 (and_1_out[9], C2, R1);
  and and_11 (and_1_out[10], C2, R2);
  and and_12 (and_1_out[11], C2, R3);
  Priority_Encoder #(.select(4)) priority_encoder_1 (
    .in0(and_1_out[0]), .in1(and_1_out[1]), .in2(and_1_out[2]), .in3(and_1_out[3]), .in4(and_1_out[4]),
    .in5(and_1_out[5]), .in6(and_1_out[6]), .in7(and_1_out[7]), .in8(and_1_out[8]), .in9(and_1_out[9]),
    .in10(and_1_out[10]), .in11(and_1_out[11]), .in12(undriven), .in13(undriven_2), .in15(undriven_3),
    .out({B3, B2, B1, B0}), .en_in(or_1_out));  // open: in14, gs, en_out
  or or_1 (or_1_out, and_1_out[0], and_1_out[1], and_1_out[2], and_1_out[3], and_1_out[4], and_1_out[5], and_1_out[6], and_1_out[7], and_1_out[8], and_1_out[9], and_1_out[10], and_1_out[11], 1'b0);
  ExactlyOne xor_1 (
    .out(V), .in0(and_1_out[0]), .in1(and_1_out[1]), .in2(and_1_out[2]), .in3(and_1_out[3]),
    .in4(and_1_out[4]), .in5(and_1_out[5]), .in6(and_1_out[6]), .in7(and_1_out[7]), .in8(and_1_out[8]),
    .in9(and_1_out[9]), .in10(and_1_out[10]), .in11(and_1_out[11]));
endmodule

module InputBuffer (
  input  B0,
  input  B1,
  input  B2,
  input  B3,
  input  V,
  input  CLK,
  output C0,
  output C1,
  output C2,
  output C3
);
endmodule

module Lock (
  input  C0,
  input  C1,
  input  C2,
  input  C3,
  input  CLK,
  output L,
  output U
);
endmodule
